// Logisim project Multiplexer1Bit.circ as structural Verilog: 1 circuit, main circuit Multiplexer1Bit
module Multiplexer1Bit (
  input  A,
  input  B,
  input  S0,
  output Multi
);

  wire and_1_out, and_2_out, not_1_out;

  not not_1 (not_1_out, S0);
  and and_1 (and_1_out, B, not_1_out);
  and and_2 (and_2_out, A, S0);
  or or_1 (Multi, and_1_out, and_2_out);
endmodule
