// Logisim project Multiplexer2Bits.circ as structural Verilog: 1 circuit, main circuit Multiplexer2Bits
module Multiplexer2Bits (
  input  [1:0] A,
  input  [1:0] B,
  input  S0,
  output [1:0] Multi
);

  Multiplexer1Bit multiplexer1bit_1 (.A(A[0]), .B(B[0]), .S0(S0), .Multi(Multi[0]));
  Multiplexer1Bit multiplexer1bit_2 (.A(A[1]), .B(B[1]), .S0(S0), .Multi(Multi[1]));
endmodule
