// Logisim project Multiplexer3Bits.circ as structural Verilog: 1 circuit, main circuit Multiplexer3Bits
module Multiplexer3Bits (
  input  [2:0] A,
  input  [2:0] B,
  input  S0,
  output [2:0] Multi
);

  Multiplexer2Bits multiplexer2bits_1 (.A(A[1:0]), .B(B[1:0]), .S0(S0), .Multi(Multi[1:0]));
  Multiplexer1Bit multiplexer1bit_1 (.A(A[2]), .B(B[2]), .S0(S0), .Multi(Multi[2]));
endmodule
