// Logisim project Multiplexer4Bits.circ as structural Verilog: 1 circuit, main circuit Multiplexer4Bits
module Multiplexer4Bits (
  input  [3:0] A,
  input  [3:0] B,
  input  S0,
  output [3:0] Multi
);

  Multiplexer2Bits multiplexer2bits_1 (.A(A[1:0]), .B(B[1:0]), .S0(S0), .Multi(Multi[1:0]));
  Multiplexer2Bits multiplexer2bits_2 (.A(A[3:2]), .B(B[3:2]), .S0(S0), .Multi(Multi[3:2]));
endmodule
