// Logisim project Multiplexer7Bits.circ as structural Verilog: 1 circuit, main circuit Multi7Bits
module Multi7Bits (
  input  [6:0] A,
  input  [6:0] B,
  input  S0,
  output [6:0] Multi
);

  Multiplexer4Bits multiplexer4bits_1 (.A(A[3:0]), .B(B[3:0]), .S0(S0), .Multi(Multi[3:0]));
  Multiplexer3Bits multiplexer3bits_1 (.A(A[6:4]), .B(B[6:4]), .S0(S0), .Multi(Multi[6:4]));
endmodule
