// Logisim project FromJoystickYToMatrix.circ as structural Verilog: 3 circuits, main circuit FromJoystickYToMatrix
module FromJoystickYToMatrix (
  input  [2:0] JoystickY,
  output [3:0] Row_0,
  output [3:0] Row_1,
  output [3:0] Row_2,
  output [3:0] Row_3,
  output [3:0] Row_4
);

  RowsZeroOne rowszeroone_1 (.JoystickY(JoystickY), .Row_0(Row_0), .Row_1(Row_1));
  RowsTwoThree rowstwothree_1 (.JoystickY(JoystickY), .Row_0(Row_2), .Row_1(Row_3));
  FifthRowY fifthrowy_1 (.JoystickY(JoystickY), .UpDir(3'b011), .DownDir(3'b111), .IdleDir(3'b010), .MatrixRow(Row_4));
endmodule

module RowsZeroOne (
  input  [2:0] JoystickY,
  output [3:0] Row_0,
  output [3:0] Row_1
);

  FirstRowY firstrowy_1 (.JoystickY(JoystickY), .UpDir(3'b011), .DownDir(3'b111), .IdleDir(3'b010), .MatrixRow(Row_0));
  SecondRowY secondrowy_1 (
    .JoystickY(JoystickY), .UpDir(3'b011), .DownDir(3'b111), .IdleDir(3'b010), .MatrixRow(Row_1));
endmodule

module RowsTwoThree (
  input  [2:0] JoystickY,
  output [3:0] Row_0,
  output [3:0] Row_1
);

  ThirdRowY thirdrowy_1 (.JoystickY(JoystickY), .UpDir(3'b011), .DownDir(3'b111), .IdleDir(3'b010), .MatrixRow(Row_0));
  FourthRowY fourthrowy_1 (
    .JoystickY(JoystickY), .UpDir(3'b011), .DownDir(3'b111), .IdleDir(3'b010), .MatrixRow(Row_1));
endmodule
