// Logisim project FromYCoordToRows.circ as structural Verilog: 5 circuits, main circuit FirstRowY
module FirstRowY (
  input  [2:0] JoystickY,
  input  [2:0] UpDir,
  input  [2:0] DownDir,
  input  [2:0] IdleDir,
  output [3:0] MatrixRow
);

  ThreeCaseSwitch4Bits threecaseswitch4bits_1 (
    .Value(JoystickY), .FirstCase(UpDir), .FirstValue(4'b1001), .SecondCase(DownDir), .SecondValue(4'b1100),
    .ThirdCase(IdleDir), .ThirdValue(4'b0111), .DEFAULT(4'b1111), .ReturnedValue(MatrixRow));
endmodule

module SecondRowY (
  input  [2:0] JoystickY,
  input  [2:0] UpDir,
  input  [2:0] DownDir,
  input  [2:0] IdleDir,
  output [3:0] MatrixRow
);

  ThreeCaseSwitch4Bits threecaseswitch4bits_1 (
    .Value(JoystickY), .FirstCase(UpDir), .FirstValue(4'b1001), .SecondCase(DownDir), .SecondValue(4'b1010),
    .ThirdCase(IdleDir), .ThirdValue(4'b1000), .DEFAULT(4'b1000), .ReturnedValue(MatrixRow));
endmodule

module ThirdRowY (
  input  [2:0] JoystickY,
  input  [2:0] UpDir,
  input  [2:0] DownDir,
  input  [2:0] IdleDir,
  output [3:0] MatrixRow
);

  ThreeCaseSwitch4Bits threecaseswitch4bits_1 (
    .Value(JoystickY), .FirstCase(UpDir), .FirstValue(4'b1001), .SecondCase(DownDir), .SecondValue(4'b1001),
    .ThirdCase(IdleDir), .ThirdValue(4'b1111), .DEFAULT(4'b1111), .ReturnedValue(MatrixRow));
endmodule

module FourthRowY (
  input  [2:0] JoystickY,
  input  [2:0] UpDir,
  input  [2:0] DownDir,
  input  [2:0] IdleDir,
  output [3:0] MatrixRow
);

  ThreeCaseSwitch4Bits threecaseswitch4bits_1 (
    .Value(JoystickY), .FirstCase(UpDir), .FirstValue(4'b1001), .SecondCase(DownDir), .SecondValue(4'b1010),
    .ThirdCase(IdleDir), .ThirdValue(4'b0001), .DEFAULT(4'b1000), .ReturnedValue(MatrixRow));
endmodule

module FifthRowY (
  input  [2:0] JoystickY,
  input  [2:0] UpDir,
  input  [2:0] DownDir,
  input  [2:0] IdleDir,
  output [3:0] MatrixRow
);

  ThreeCaseSwitch4Bits threecaseswitch4bits_1 (
    .Value(JoystickY), .FirstCase(UpDir), .FirstValue(4'b1111), .SecondCase(DownDir), .SecondValue(4'b1100),
    .ThirdCase(IdleDir), .ThirdValue(4'b1110), .DEFAULT(4'b1111), .ReturnedValue(MatrixRow));
endmodule
