// Logisim project Equality.circ as structural Verilog: 3 circuits, main circuit Equality1Bit
module Equality1Bit (
  input  A,
  input  B,
  output EQAB
);

  wire and_1_out, and_2_out, not_1_out, not_2_out;

  not not_1 (not_1_out, A);
  not not_2 (not_2_out, B);
  and and_1 (and_1_out, B, A);
  and and_2 (and_2_out, not_1_out, not_2_out);
  or or_1 (EQAB, and_1_out, and_2_out);
endmodule

module Equality2Bits (
  input  [1:0] A,
  input  [1:0] B,
  output EQAB
);

  wire equality1bit_1_eqab, equality1bit_2_eqab;

  Equality1Bit equality1bit_1 (.A(A[0]), .B(B[0]), .EQAB(equality1bit_1_eqab));
  Equality1Bit equality1bit_2 (.A(A[1]), .B(B[1]), .EQAB(equality1bit_2_eqab));
  and and_1 (EQAB, equality1bit_1_eqab, equality1bit_2_eqab);
endmodule

module Equality3Bits (
  input  [2:0] A,
  input  [2:0] B,
  output AQAB
);

  wire equality1bit_1_eqab, equality2bits_1_eqab;

  Equality1Bit equality1bit_1 (.A(A[2]), .B(B[2]), .EQAB(equality1bit_1_eqab));
  Equality2Bits equality2bits_1 (.A(A[1:0]), .B(B[1:0]), .EQAB(equality2bits_1_eqab));
  and and_1 (AQAB, equality1bit_1_eqab, equality2bits_1_eqab);
endmodule
