// Logisim project FromJoystickXToMatrix.circ as structural Verilog: 3 circuits, main circuit FromJoystickXToMatrix
module FromJoystickXToMatrix (
  input  [2:0] JoystickX,
  output [3:0] Row_0,
  output [3:0] Row_1,
  output [3:0] Row_2,
  output [3:0] Row_3,
  output [3:0] Row_4
);

  RowsZeroOne rowszeroone_1 (.JoystickX(JoystickX), .Row_0(Row_0), .Row_1(Row_1));
  RowsTwoThree rowstwothree_1 (.JoystickX(JoystickX), .Row_2(Row_2), .Row_3(Row_3));
  FifthRowX fifthrowx_1 (
    .JoystickX(JoystickX), .RightDir(3'b101), .LeftDir(3'b000), .IdleDir(3'b010), .MatrixRow(Row_4));
endmodule

module RowsZeroOne (
  input  [2:0] JoystickX,
  output [3:0] Row_0,
  output [3:0] Row_1
);

  FirstRowX firstrowx_1 (
    .JoystickX(JoystickX), .RightDir(3'b101), .LeftDir(3'b000), .IdleDir(3'b010), .MatrixRow(Row_0));
  SecondRowX secondrowx_1 (
    .JoystickX(JoystickX), .RightDir(3'b101), .LeftDir(3'b000), .IdleDir(3'b010), .MatrixRow(Row_1));
endmodule

module RowsTwoThree (
  input  [2:0] JoystickX,
  output [3:0] Row_2,
  output [3:0] Row_3
);

  ThirdRowX thirdrowx_1 (
    .JoystickX(JoystickX), .RightDir(3'b101), .LeftDir(3'b000), .IdleDir(3'b010), .MatrixRow(Row_2));
  FourthRowX fourthrowx_1 (
    .JoystickX(JoystickX), .RightDir(3'b101), .LeftDir(3'b000), .IdleDir(3'b010), .MatrixRow(Row_3));
endmodule
