// Logisim project FromXCoordToRows.circ as structural Verilog: 5 circuits, main circuit FirstRowX
module FirstRowX (
  input  [2:0] JoystickX,
  input  [2:0] RightDir,
  input  [2:0] LeftDir,
  input  [2:0] IdleDir,
  output [3:0] MatrixRow
);

  ThreeCaseSwitch4Bits threecaseswitch4bits_1 (
    .Value(JoystickX), .FirstCase(RightDir), .FirstValue(4'b1110), .SecondCase(LeftDir),
    .SecondValue(4'b1000), .ThirdCase(IdleDir), .ThirdValue(4'b0111), .DefaultValue(4'b1111),
    .ReturnedValue(MatrixRow));
endmodule

module SecondRowX (
  input  [2:0] JoystickX,
  input  [2:0] RightDir,
  input  [2:0] LeftDir,
  input  [2:0] IdleDir,
  output [3:0] MatrixRow
);

  ThreeCaseSwitch4Bits threecaseswitch4bits_1 (
    .Value(JoystickX), .FirstCase(RightDir), .FirstValue(4'b1001), .SecondCase(LeftDir),
    .SecondValue(4'b1000), .ThirdCase(IdleDir), .ThirdValue(4'b1000), .DefaultValue(4'b1000),
    .ReturnedValue(MatrixRow));
endmodule

module ThirdRowX (
  input  [2:0] JoystickX,
  input  [2:0] RightDir,
  input  [2:0] LeftDir,
  input  [2:0] IdleDir,
  output [3:0] MatrixRow
);

  ThreeCaseSwitch4Bits threecaseswitch4bits_1 (
    .Value(JoystickX), .FirstCase(RightDir), .FirstValue(4'b1110), .SecondCase(LeftDir),
    .SecondValue(4'b1000), .ThirdCase(IdleDir), .ThirdValue(4'b1111), .DefaultValue(4'b1111),
    .ReturnedValue(MatrixRow));
endmodule

module FourthRowX (
  input  [2:0] JoystickX,
  input  [2:0] RightDir,
  input  [2:0] LeftDir,
  input  [2:0] IdleDir,
  output [3:0] MatrixRow
);

  ThreeCaseSwitch4Bits threecaseswitch4bits_1 (
    .Value(JoystickX), .FirstCase(RightDir), .FirstValue(4'b1010), .SecondCase(LeftDir),
    .SecondValue(4'b1000), .ThirdCase(IdleDir), .ThirdValue(4'b0001), .DefaultValue(4'b1000),
    .ReturnedValue(MatrixRow));
endmodule

module FifthRowX (
  input  [2:0] JoystickX,
  input  [2:0] RightDir,
  input  [2:0] LeftDir,
  input  [2:0] IdleDir,
  output [3:0] MatrixRow
);

  ThreeCaseSwitch4Bits threecaseswitch4bits_1 (
    .Value(JoystickX), .FirstCase(RightDir), .FirstValue(4'b1001), .SecondCase(LeftDir),
    .SecondValue(4'b1111), .ThirdCase(IdleDir), .ThirdValue(4'b1110), .DefaultValue(4'b1111),
    .ReturnedValue(MatrixRow));
endmodule
