// Logisim project Switch.circ as structural Verilog: 1 circuit, main circuit ThreeCaseSwitch4Bits
module ThreeCaseSwitch4Bits (
  input  [2:0] Value,
  input  [2:0] FirstCase,
  input  [3:0] FirstValue,
  input  [2:0] SecondCase,
  input  [3:0] SecondValue,
  input  [2:0] ThirdCase,
  input  [3:0] ThirdValue,
  input  [3:0] DefaultValue,
  output [3:0] ReturnedValue
);

  wire equality3bits_1_aqab, equality3bits_2_aqab, equality3bits_3_aqab;
  wire [3:0] ifthenelsefourbits_1_c, ifthenelsefourbits_2_c;

  Equality3Bits equality3bits_1 (.A(Value), .B(SecondCase), .AQAB(equality3bits_1_aqab));
  Equality3Bits equality3bits_2 (.A(Value), .B(ThirdCase), .AQAB(equality3bits_2_aqab));
  Equality3Bits equality3bits_3 (.A(Value), .B(FirstCase), .AQAB(equality3bits_3_aqab));
  IfThenElseFourBits ifthenelsefourbits_1 (
    .COND(equality3bits_2_aqab), .A(ThirdValue), .B(DefaultValue), .C(ifthenelsefourbits_1_c));
  IfThenElseFourBits ifthenelsefourbits_2 (
    .COND(equality3bits_1_aqab), .A(SecondValue), .B(ifthenelsefourbits_1_c), .C(ifthenelsefourbits_2_c));
  IfThenElseFourBits ifthenelsefourbits_3 (
    .COND(equality3bits_3_aqab), .A(FirstValue), .B(ifthenelsefourbits_2_c), .C(ReturnedValue));
endmodule
