// Logisim project RC_Controller.circ as structural Verilog: 1 circuit, main circuit RC_Controller
module RC_Controller (
);

  wire buttonspeedsystem_1_a, buttonspeedsystem_1_b, buttonspeedsystem_1_c, buttonspeedsystem_1_d,
       buttonspeedsystem_1_e, buttonspeedsystem_1_f, buttonspeedsystem_1_g, D_out, U_out;
  wire [2:0] bitselector_1_out, bitselector_2_out, bitselector_3_out, bitselector_4_out;
  wire [3:0] joystick_1_x, joystick_1_y, joystick_2_x, joystick_2_y, joysticksystem_1_row_0,
       joysticksystem_1_row_0_2, joysticksystem_1_row_1, joysticksystem_1_row_1_2, joysticksystem_1_row_2,
       joysticksystem_1_row_2_2, joysticksystem_1_row_3, joysticksystem_1_row_3_2, joysticksystem_1_row_4,
       joysticksystem_1_row_4_2, joysticksystem_2_row_0, joysticksystem_2_row_0_2, joysticksystem_2_row_1,
       joysticksystem_2_row_1_2, joysticksystem_2_row_2, joysticksystem_2_row_2_2, joysticksystem_2_row_3,
       joysticksystem_2_row_3_2, joysticksystem_2_row_4, joysticksystem_2_row_4_2;

  Joystick joystick_1 (.x(joystick_1_x), .y(joystick_1_y));
  Joystick joystick_2 (.x(joystick_2_x), .y(joystick_2_y));
  BitSelector #(.width(4), .group(3)) bitselector_1 (.in(joystick_1_x), .out(bitselector_1_out), .sel(1'b0));
  BitSelector #(.width(4), .group(3)) bitselector_2 (.in(joystick_1_y), .out(bitselector_2_out), .sel(1'b0));
  Button U (.out(U_out));
  Button D (.out(D_out));
  BitSelector #(.width(4), .group(3)) bitselector_3 (.in(joystick_2_x), .out(bitselector_3_out), .sel(1'b0));
  BitSelector #(.width(4), .group(3)) bitselector_4 (.in(joystick_2_y), .out(bitselector_4_out), .sel(1'b0));
  JoystickSystem joysticksystem_1 (
    .JoystickX(bitselector_1_out), .JoystickY(bitselector_2_out), .Row_0(joysticksystem_1_row_0),
    .Row_1(joysticksystem_1_row_1), .Row_2(joysticksystem_1_row_2), .Row_3(joysticksystem_1_row_3),
    .Row_4(joysticksystem_1_row_4), .Row_0_2(joysticksystem_1_row_0_2), .Row_1_2(joysticksystem_1_row_1_2),
    .Row_2_2(joysticksystem_1_row_2_2), .Row_3_2(joysticksystem_1_row_3_2), .Row_4_2(joysticksystem_1_row_4_2));
  ButtonSpeedSystem buttonspeedsystem_1 (
    .in_1(U_out), .in_2(D_out), .a(buttonspeedsystem_1_a), .b(buttonspeedsystem_1_b),
    .c(buttonspeedsystem_1_c), .d(buttonspeedsystem_1_d), .e(buttonspeedsystem_1_e),
    .f(buttonspeedsystem_1_f), .g(buttonspeedsystem_1_g));
  JoystickSystem joysticksystem_2 (
    .JoystickX(bitselector_3_out), .JoystickY(bitselector_4_out), .Row_0(joysticksystem_2_row_0),
    .Row_1(joysticksystem_2_row_1), .Row_2(joysticksystem_2_row_2), .Row_3(joysticksystem_2_row_3),
    .Row_4(joysticksystem_2_row_4), .Row_0_2(joysticksystem_2_row_0_2), .Row_1_2(joysticksystem_2_row_1_2),
    .Row_2_2(joysticksystem_2_row_2_2), .Row_3_2(joysticksystem_2_row_3_2), .Row_4_2(joysticksystem_2_row_4_2));
  DotMatrix #(.inputtype("row"), .matrixcols(4), .matrixrows(5)) dotmatrix_1 (
    .row0(joysticksystem_1_row_0), .row1(joysticksystem_1_row_1), .row2(joysticksystem_1_row_2),
    .row3(joysticksystem_1_row_3), .row4(joysticksystem_1_row_4));
  DotMatrix #(.inputtype("row"), .matrixcols(4), .matrixrows(5)) dotmatrix_2 (
    .row0(joysticksystem_1_row_0_2), .row1(joysticksystem_1_row_1_2), .row2(joysticksystem_1_row_2_2),
    .row3(joysticksystem_1_row_3_2), .row4(joysticksystem_1_row_4_2));
  _7_Segment_Display u_7_segment_display_1 (
    .g(buttonspeedsystem_1_g), .f(buttonspeedsystem_1_f), .a(buttonspeedsystem_1_a),
    .b(buttonspeedsystem_1_b), .e(buttonspeedsystem_1_e), .d(buttonspeedsystem_1_d), .c(buttonspeedsystem_1_c));  // open: dp
  DotMatrix #(.inputtype("row"), .matrixcols(4), .matrixrows(5)) dotmatrix_3 (
    .row0(joysticksystem_2_row_0), .row1(joysticksystem_2_row_1), .row2(joysticksystem_2_row_2),
    .row3(joysticksystem_2_row_3), .row4(joysticksystem_2_row_4));
  DotMatrix #(.inputtype("row"), .matrixcols(4), .matrixrows(5)) dotmatrix_4 (
    .row0(joysticksystem_2_row_0_2), .row1(joysticksystem_2_row_1_2), .row2(joysticksystem_2_row_2_2),
    .row3(joysticksystem_2_row_3_2), .row4(joysticksystem_2_row_4_2));

  // Notes on the sheet:
  //   Ailerions
  //   SpeedButtons
  //   Elevators
endmodule
