// Logisim project MultiPlexer.circ as structural Verilog: 5 circuits, main circuit Multiplexer1Bit
module Multiplexer1Bit (
  input  A,
  input  B,
  input  S0,
  output Multi
);

  wire and_1_out, and_2_out, not_1_out;

  not not_1 (not_1_out, S0);
  and and_1 (and_1_out, B, not_1_out);
  and and_2 (and_2_out, A, S0);
  or or_1 (Multi, and_1_out, and_2_out);
endmodule

module Multiplexer2Bits (
  input  [1:0] A,
  input  [1:0] B,
  input  S0,
  output [1:0] Multi
);

  Multiplexer1Bit multiplexer1bit_1 (.A(A[0]), .B(B[0]), .S0(S0), .Multi(Multi[0]));
  Multiplexer1Bit multiplexer1bit_2 (.A(A[1]), .B(B[1]), .S0(S0), .Multi(Multi[1]));
endmodule

module Multiplexer3Bits (
  input  [2:0] A,
  input  [2:0] B,
  input  S0,
  output [2:0] Multi
);

  Multiplexer2Bits multiplexer2bits_1 (.A(A[1:0]), .B(B[1:0]), .S0(S0), .Multi(Multi[1:0]));
  Multiplexer1Bit multiplexer1bit_1 (.A(A[2]), .B(B[2]), .S0(S0), .Multi(Multi[2]));
endmodule

module Multiplexer4Bits (
  input  [3:0] A,
  input  [3:0] B,
  input  S0,
  output [3:0] Multi
);

  Multiplexer2Bits multiplexer2bits_1 (.A(A[1:0]), .B(B[1:0]), .S0(S0), .Multi(Multi[1:0]));
  Multiplexer2Bits multiplexer2bits_2 (.A(A[3:2]), .B(B[3:2]), .S0(S0), .Multi(Multi[3:2]));
endmodule

module Multi7Bits (
  input  [6:0] A,
  input  [6:0] B,
  input  S0,
  output [6:0] Multi
);

  Multiplexer4Bits multiplexer4bits_1 (.A(A[3:0]), .B(B[3:0]), .S0(S0), .Multi(Multi[3:0]));
  Multiplexer3Bits multiplexer3bits_1 (.A(A[6:4]), .B(B[6:4]), .S0(S0), .Multi(Multi[6:4]));
endmodule
