// Logisim project Adder.circ as structural Verilog: 4 circuits, main circuit Adder1Bit
module Adder1Bit (
  input  A,
  input  B,
  input  CIN,
  output S,
  output COUT
);

  wire and_1_out, and_2_out, and_3_out, xor_1_out;

  xor xor_1 (xor_1_out, A, B);
  and and_1 (and_1_out, B, A);
  and and_2 (and_2_out, CIN, A);
  and and_3 (and_3_out, CIN, B);
  xor xor_2 (S, xor_1_out, CIN);
  or or_1 (COUT, and_1_out, and_2_out, and_3_out);
endmodule

module Adder2bits (
  input  [1:0] A,
  input  [1:0] B,
  output [1:0] out_3,
  output COUT
);

  wire adder1bit_1_cout, bitselector_1_out, bitselector_2_out, bitselector_3_out, bitselector_4_out;

  BitSelector #(.width(2)) bitselector_1 (.in(A), .out(bitselector_1_out), .sel(1'b1));
  BitSelector #(.width(2)) bitselector_2 (.in(A), .out(bitselector_2_out), .sel(1'b0));
  BitSelector #(.width(2)) bitselector_3 (.in(B), .out(bitselector_3_out), .sel(1'b0));
  BitSelector #(.width(2)) bitselector_4 (.in(B), .out(bitselector_4_out), .sel(1'b1));
  Adder1Bit adder1bit_1 (
    .A(bitselector_2_out), .B(bitselector_3_out), .CIN(1'b0), .S(out_3[0]), .COUT(adder1bit_1_cout));
  Adder1Bit adder1bit_2 (
    .A(bitselector_1_out), .B(bitselector_4_out), .CIN(adder1bit_1_cout), .S(out_3[1]), .COUT(COUT));
endmodule

module Adder3Bits (
  input  [2:0] A,
  input  [2:0] B,
  output [2:0] S,
  output COUT
);

  wire adder2bits_1_cout, bitselector_3_out, bitselector_4_out;
  wire [1:0] bitselector_1_out, bitselector_2_out;

  BitSelector #(.width(3), .group(2)) bitselector_1 (.in(A), .out(bitselector_1_out), .sel(1'b0));
  BitSelector #(.width(3), .group(2)) bitselector_2 (.in(B), .out(bitselector_2_out), .sel(1'b0));
  Adder2bits adder2bits_1 (.A(bitselector_1_out), .B(bitselector_2_out), .out_3(S[1:0]), .COUT(adder2bits_1_cout));
  BitSelector #(.width(3)) bitselector_3 (.in(A), .out(bitselector_3_out), .sel(2'b10));
  BitSelector #(.width(3)) bitselector_4 (.in(B), .out(bitselector_4_out), .sel(2'b10));
  Adder1Bit adder1bit_1 (.A(bitselector_3_out), .B(bitselector_4_out), .CIN(adder2bits_1_cout), .S(S[2]), .COUT(COUT));
endmodule

module Adder4Bits (
  input  [3:0] A,
  input  [3:0] B,
  output [3:0] S,
  output COUT
);

  wire adder3bits_1_cout, bitselector_3_out, bitselector_4_out;
  wire [2:0] bitselector_1_out, bitselector_2_out;

  BitSelector #(.width(4), .group(3)) bitselector_1 (.in(A), .out(bitselector_1_out), .sel(1'b0));
  BitSelector #(.width(4), .group(3)) bitselector_2 (.in(B), .out(bitselector_2_out), .sel(1'b0));
  Adder3Bits adder3bits_1 (.A(bitselector_1_out), .B(bitselector_2_out), .S(S[2:0]), .COUT(adder3bits_1_cout));
  BitSelector #(.width(4)) bitselector_3 (.in(A), .out(bitselector_3_out), .sel(2'b11));
  BitSelector #(.width(4)) bitselector_4 (.in(B), .out(bitselector_4_out), .sel(2'b11));
  Adder1Bit adder1bit_1 (.A(bitselector_3_out), .B(bitselector_4_out), .CIN(adder3bits_1_cout), .S(S[3]), .COUT(COUT));
endmodule
