// Logisim project SpeedController.circ as structural Verilog: 1 circuit, main circuit SpeedController
module SpeedController (
  input  U,
  input  D,
  output [2:0] Speed
);

  wire clock_1_out;
  wire [2:0] register_1_q;

  Register #(.width(3)) register_1 (.D(Speed), .Q(register_1_q), .clk(clock_1_out));  // open: en, clr
  Clock clock_1 (.out(clock_1_out));
  SpeedAdder speedadder_1 (
    .J2(register_1_q[2]), .J1(register_1_q[1]), .J0(register_1_q[0]), .U(U), .D(D), .D2(Speed[2]),
    .D1(Speed[1]), .D0(Speed[0]));
endmodule
