// Logisim project Equality.circ as structural Verilog: 4 circuits, main circuit Equality1Bit
module Equality2Bits (
  input  [1:0] A,
  input  [1:0] B,
  output EQAB
);

  wire equality1bit_1_eqab, equality1bit_2_eqab;

  Equality1Bit equality1bit_1 (.A(A[1]), .B(B[1]), .EQAB(equality1bit_1_eqab));
  Equality1Bit equality1bit_2 (.A(A[0]), .B(B[0]), .EQAB(equality1bit_2_eqab));
  and and_1 (EQAB, equality1bit_1_eqab, equality1bit_2_eqab);
endmodule

module Equality1Bit (
  input  A,
  input  B,
  output EQAB
);

  wire xor_1_xor;

  XOR xor_1 (.A(A), .B(B), .XOR(xor_1_xor));
  not not_1 (EQAB, xor_1_xor);
endmodule

module Equality3Bits (
  input  [2:0] A,
  input  [2:0] B,
  output AQAB
);

  wire equality1bit_1_eqab, equality1bit_2_eqab, equality1bit_3_eqab;

  Equality1Bit equality1bit_1 (.A(A[1]), .B(B[1]), .EQAB(equality1bit_1_eqab));
  Equality1Bit equality1bit_2 (.A(A[2]), .B(B[2]), .EQAB(equality1bit_2_eqab));
  Equality1Bit equality1bit_3 (.A(A[0]), .B(B[0]), .EQAB(equality1bit_3_eqab));
  and and_1 (AQAB, equality1bit_2_eqab, equality1bit_3_eqab, equality1bit_1_eqab);
endmodule

module Equality4Bits (
  input  [3:0] A,
  input  [3:0] B,
  output AQAB
);

  wire equality1bit_1_eqab, equality1bit_2_eqab, equality1bit_3_eqab, equality1bit_4_eqab;

  Equality1Bit equality1bit_1 (.A(A[3]), .B(B[3]), .EQAB(equality1bit_1_eqab));
  Equality1Bit equality1bit_2 (.A(A[2]), .B(B[2]), .EQAB(equality1bit_2_eqab));
  Equality1Bit equality1bit_3 (.A(A[1]), .B(B[1]), .EQAB(equality1bit_3_eqab));
  Equality1Bit equality1bit_4 (.A(A[0]), .B(B[0]), .EQAB(equality1bit_4_eqab));
  and and_1 (AQAB, equality1bit_2_eqab, equality1bit_4_eqab, equality1bit_1_eqab, equality1bit_3_eqab);
endmodule
