// Logisim project FromJoystickYToMatrix.circ as structural Verilog: 8 circuits, main circuit FirstRowY
module FirstRowY (
  input  [2:0] JoystickY,
  input  [2:0] UpDir,
  input  [2:0] DownDir,
  input  [2:0] IdleDir,
  output [3:0] MatrixRow
);

  ThreeCaseSwitch4Bits threecaseswitch4bits_1 (
    .Value(JoystickY), .FirstCase(UpDir), .FirstValue(4'b1001), .SecondCase(DownDir), .SecondValue(4'b1100),
    .ThirdCase(IdleDir), .ThirdValue(4'b0111), .DEFAULT(4'b1111), .ReturnedValue(MatrixRow));
endmodule

module SecondRowY (
  input  [2:0] JoystickY,
  input  [2:0] UpDir,
  input  [2:0] DownDir,
  input  [2:0] IdleDir,
  output [3:0] MatrixRow
);

  ThreeCaseSwitch4Bits threecaseswitch4bits_1 (
    .Value(JoystickY), .FirstCase(UpDir), .FirstValue(4'b1001), .SecondCase(DownDir), .SecondValue(4'b1010),
    .ThirdCase(IdleDir), .ThirdValue(4'b1000), .DEFAULT(4'b1000), .ReturnedValue(MatrixRow));
endmodule

module ThirdRowY (
  input  [2:0] JoystickY,
  input  [2:0] UpDir,
  input  [2:0] DownDir,
  input  [2:0] IdleDir,
  output [3:0] MatrixRow
);

  ThreeCaseSwitch4Bits threecaseswitch4bits_1 (
    .Value(JoystickY), .FirstCase(UpDir), .FirstValue(4'b1001), .SecondCase(DownDir), .SecondValue(4'b1001),
    .ThirdCase(IdleDir), .ThirdValue(4'b1111), .DEFAULT(4'b1111), .ReturnedValue(MatrixRow));
endmodule

module FourthRowY (
  input  [2:0] JoystickY,
  input  [2:0] UpDir,
  input  [2:0] DownDir,
  input  [2:0] IdleDir,
  output [3:0] MatrixRow
);

  ThreeCaseSwitch4Bits threecaseswitch4bits_1 (
    .Value(JoystickY), .FirstCase(UpDir), .FirstValue(4'b1001), .SecondCase(DownDir), .SecondValue(4'b1010),
    .ThirdCase(IdleDir), .ThirdValue(4'b0001), .DEFAULT(4'b1000), .ReturnedValue(MatrixRow));
endmodule

module FifthRowY (
  input  [2:0] JoystickY,
  input  [2:0] UpDir,
  input  [2:0] DownDir,
  input  [2:0] IdleDir,
  output [3:0] MatrixRow
);

  ThreeCaseSwitch4Bits threecaseswitch4bits_1 (
    .Value(JoystickY), .FirstCase(UpDir), .FirstValue(4'b1111), .SecondCase(DownDir), .SecondValue(4'b1100),
    .ThirdCase(IdleDir), .ThirdValue(4'b1110), .DEFAULT(4'b1111), .ReturnedValue(MatrixRow));
endmodule

module RowsZeroOne (
  input  [2:0] JoystickY,
  output [3:0] Row_0,
  output [3:0] Row_1
);

  FirstRowY firstrowy_1 (.JoystickY(JoystickY), .UpDir(3'b011), .DownDir(3'b111), .IdleDir(3'b010), .MatrixRow(Row_0));
  SecondRowY secondrowy_1 (
    .JoystickY(JoystickY), .UpDir(3'b011), .DownDir(3'b111), .IdleDir(3'b010), .MatrixRow(Row_1));
endmodule

module RowsTwoThree (
  input  [2:0] JoystickY,
  output [3:0] Row_0,
  output [3:0] Row_1
);

  ThirdRowY thirdrowy_1 (.JoystickY(JoystickY), .UpDir(3'b011), .DownDir(3'b111), .IdleDir(3'b010), .MatrixRow(Row_0));
  FourthRowY fourthrowy_1 (
    .JoystickY(JoystickY), .UpDir(3'b011), .DownDir(3'b111), .IdleDir(3'b010), .MatrixRow(Row_1));
endmodule

module FromJoystickYToMatrix (
  input  [2:0] JoystickY,
  output [3:0] Row_0,
  output [3:0] Row_1,
  output [3:0] Row_2,
  output [3:0] Row_3,
  output [3:0] Row_4
);

  RowsZeroOne rowszeroone_1 (.JoystickY(JoystickY), .Row_0(Row_0), .Row_1(Row_1));
  RowsTwoThree rowstwothree_1 (.JoystickY(JoystickY), .Row_0(Row_2), .Row_1(Row_3));
  FifthRowY fifthrowy_1 (.JoystickY(JoystickY), .UpDir(3'b011), .DownDir(3'b111), .IdleDir(3'b010), .MatrixRow(Row_4));
endmodule
