// Logisim project JoystickSystem.circ as structural Verilog: 1 circuit, main circuit JoystickSystem
module JoystickSystem (
  input  [2:0] JoystickX,
  input  [2:0] JoystickY,
  output [3:0] Row_0,
  output [3:0] Row_1,
  output [3:0] Row_2,
  output [3:0] Row_3,
  output [3:0] Row_4,
  output [3:0] Row_0_2,
  output [3:0] Row_1_2,
  output [3:0] Row_2_2,
  output [3:0] Row_3_2,
  output [3:0] Row_4_2
);

  FromJoystickXToMatrix fromjoystickxtomatrix_1 (
    .JoystickX(JoystickX), .Row_0(Row_0), .Row_1(Row_1), .Row_2(Row_2), .Row_3(Row_3), .Row_4(Row_4));
  FromJoystickYToMatrix fromjoystickytomatrix_1 (
    .JoystickY(JoystickY), .Row_0(Row_0_2), .Row_1(Row_1_2), .Row_2(Row_2_2), .Row_3(Row_3_2), .Row_4(Row_4_2));
endmodule
