// Logisim project Switch.circ as structural Verilog: 4 circuits, main circuit SwitchThreeCase7Bit
module SwitchThreeCase7Bit (
  input  [2:0] Value,
  input  [2:0] FirstCase,
  input  [6:0] FirstValue,
  input  [2:0] SecondCase,
  input  [6:0] SecondValue,
  input  [2:0] ThirdCase,
  input  [6:0] ThirdValue,
  input  [6:0] DEFAULT,
  output [6:0] ReturnedValue
);

  wire equality3bits_1_aqab, equality3bits_2_aqab, equality3bits_3_aqab;
  wire [6:0] multi7bits_1_multi, multi7bits_2_multi;

  Equality3Bits equality3bits_1 (.A(Value), .B(FirstCase), .AQAB(equality3bits_1_aqab));
  Equality3Bits equality3bits_2 (.A(Value), .B(SecondCase), .AQAB(equality3bits_2_aqab));
  Equality3Bits equality3bits_3 (.A(Value), .B(ThirdCase), .AQAB(equality3bits_3_aqab));
  Multi7Bits multi7bits_1 (.A(ThirdValue), .B(DEFAULT), .S0(equality3bits_3_aqab), .Multi(multi7bits_1_multi));
  Multi7Bits multi7bits_2 (
    .A(SecondValue), .B(multi7bits_1_multi), .S0(equality3bits_2_aqab), .Multi(multi7bits_2_multi));
  Multi7Bits multi7bits_3 (.A(FirstValue), .B(multi7bits_2_multi), .S0(equality3bits_1_aqab), .Multi(ReturnedValue));
endmodule

module SwitchOneCase7Bits (
  input  [2:0] Value,
  input  [2:0] FirstCase,
  input  [6:0] FirstValue,
  input  [6:0] DEFAULT,
  output [6:0] ReturnedValue
);

  wire equality3bits_1_aqab;

  Equality3Bits equality3bits_1 (.A(Value), .B(FirstCase), .AQAB(equality3bits_1_aqab));
  Multi7Bits multi7bits_1 (.A(FirstValue), .B(DEFAULT), .S0(equality3bits_1_aqab), .Multi(ReturnedValue));
endmodule

module ThreeCaseSwitch4Bits (
  input  [2:0] Value,
  input  [2:0] FirstCase,
  input  [3:0] FirstValue,
  input  [2:0] SecondCase,
  input  [3:0] SecondValue,
  input  [2:0] ThirdCase,
  input  [3:0] ThirdValue,
  input  [3:0] DEFAULT,
  output [3:0] ReturnedValue
);

  wire equality3bits_1_aqab, equality3bits_2_aqab, equality3bits_3_aqab;
  wire [3:0] multiplexer4bits_1_multi, multiplexer4bits_2_multi;

  Equality3Bits equality3bits_1 (.A(Value), .B(FirstCase), .AQAB(equality3bits_1_aqab));
  Equality3Bits equality3bits_2 (.A(Value), .B(SecondCase), .AQAB(equality3bits_2_aqab));
  Equality3Bits equality3bits_3 (.A(Value), .B(ThirdCase), .AQAB(equality3bits_3_aqab));
  Multiplexer4Bits multiplexer4bits_1 (
    .A(ThirdValue), .B(DEFAULT), .S0(equality3bits_3_aqab), .Multi(multiplexer4bits_1_multi));
  Multiplexer4Bits multiplexer4bits_2 (
    .A(SecondValue), .B(multiplexer4bits_1_multi), .S0(equality3bits_2_aqab), .Multi(multiplexer4bits_2_multi));
  Multiplexer4Bits multiplexer4bits_3 (
    .A(FirstValue), .B(multiplexer4bits_2_multi), .S0(equality3bits_1_aqab), .Multi(ReturnedValue));
endmodule

module SwitchOneCase4Bits (
  input  [2:0] Value,
  input  [2:0] FirstCase,
  input  [3:0] FirstValue,
  input  [3:0] DEFAULT,
  output [3:0] ReturnedValue
);

  wire equality3bits_1_aqab;

  Equality3Bits equality3bits_1 (.A(Value), .B(FirstCase), .AQAB(equality3bits_1_aqab));
  Multiplexer4Bits multiplexer4bits_1 (.A(FirstValue), .B(DEFAULT), .S0(equality3bits_1_aqab), .Multi(ReturnedValue));
endmodule
