// Logisim project Adder1Bit.circ as structural Verilog: 1 circuit, main circuit Adder1Bit
module Adder1Bit (
  input  A,
  input  B,
  input  CIN,
  output S,
  output COUT
);

  wire and_1_out, and_2_out, and_3_out, xor_1_out;

  xor xor_1 (xor_1_out, A, B);
  and and_1 (and_1_out, B, A);
  and and_2 (and_2_out, CIN, A);
  and and_3 (and_3_out, CIN, B);
  xor xor_2 (S, xor_1_out, CIN);
  or or_1 (COUT, and_1_out, and_2_out, and_3_out);
endmodule
