// Logisim project ButtonInput.circ as structural Verilog: 1 circuit, main circuit ButtonInput
module ButtonInput (
  input  U,
  input  D,
  output D1,
  output D0
);

  wire and_2_out, and_3_out, not_1_out, not_2_out, not_3_out;

  not not_1 (not_1_out, U);
  not not_2 (not_2_out, U);
  not not_3 (not_3_out, D);
  and and_1 (D1, not_1_out, D);
  and and_2 (and_2_out, not_2_out, D);
  and and_3 (and_3_out, U, not_3_out);
  or or_1 (D0, and_2_out, and_3_out);
endmodule
