// Logisim project ButtonInputConverter.circ as structural Verilog: 1 circuit, main circuit ButtonInputConverter
module ButtonInputConverter (
  input  [1:0] Button,
  output [3:0] Conversion
);

  wire bitselector_1_out, bitselector_2_out, equality1bit_1_eqab, equality1bit_2_eqab;
  wire [3:0] multiplexer_2_out;

  BitSelector #(.width(2)) bitselector_1 (.in(Button), .out(bitselector_1_out), .sel(1'b1));
  BitSelector #(.width(2)) bitselector_2 (.in(Button), .out(bitselector_2_out), .sel(1'b0));
  Equality1Bit equality1bit_1 (.A(bitselector_1_out), .B(1'b1), .EQAB(equality1bit_1_eqab));
  Equality1Bit equality1bit_2 (.A(bitselector_2_out), .B(1'b1), .EQAB(equality1bit_2_eqab));
  Multiplexer #(.width(4)) multiplexer_1 (
    .in0(multiplexer_2_out), .in1(4'b1111), .out(Conversion), .sel(equality1bit_1_eqab));  // open: en
  Multiplexer #(.width(4)) multiplexer_2 (
    .in0(4'b0000), .in1(4'b0001), .out(multiplexer_2_out), .sel(equality1bit_2_eqab));  // open: en
endmodule
