// Logisim project ButtonSpeed.circ as structural Verilog: 1 circuit, main circuit ButtonSpeed
module ButtonSpeed (
  input  D2,
  input  D1,
  input  D0,
  input  U,
  input  D,
  output S2,
  output S1,
  output S0
);

  wire and_1_out, and_2_out, and_3_out, and_4_out, and_5_out, and_6_out, and_7_out, and_8_out, and_9_out,
       and_10_out, and_11_out, and_12_out, and_13_out, and_14_out, and_15_out, and_16_out, and_17_out,
       not_1_out, not_2_out, not_3_out, not_4_out, not_5_out, not_6_out, not_7_out, not_8_out, not_9_out,
       not_10_out, not_11_out, not_12_out, not_13_out, not_14_out, not_15_out, not_16_out, not_17_out,
       not_18_out, not_19_out, not_20_out;

  not not_1 (not_1_out, D);
  not not_2 (not_2_out, D);
  not not_3 (not_3_out, D1);
  not not_4 (not_4_out, D);
  not not_5 (not_5_out, D0);
  not not_6 (not_6_out, D);
  not not_7 (not_7_out, U);
  not not_8 (not_8_out, D1);
  not not_9 (not_9_out, D0);
  not not_10 (not_10_out, U);
  not not_11 (not_11_out, D);
  not not_12 (not_12_out, D0);
  not not_13 (not_13_out, D);
  not not_14 (not_14_out, U);
  not not_15 (not_15_out, D);
  not not_16 (not_16_out, D0);
  not not_17 (not_17_out, U);
  not not_18 (not_18_out, D0);
  not not_19 (not_19_out, U);
  not not_20 (not_20_out, D);
  and and_1 (and_1_out, D1, D0, U, not_1_out);
  and and_2 (and_2_out, D2, not_2_out);
  and and_3 (and_3_out, D2, U);
  and and_4 (and_4_out, D2, D0);
  and and_5 (and_5_out, D2, D1);
  and and_6 (and_6_out, not_3_out, D0, U, not_4_out);
  and and_7 (and_7_out, D1, not_5_out, not_6_out);
  and and_8 (and_8_out, D1, U, D);
  and and_9 (and_9_out, D1, D0, not_7_out);
  and and_10 (and_10_out, D2, not_8_out, not_9_out, not_10_out, D);
  and and_11 (and_11_out, D2, D1, not_11_out);
  and and_12 (and_12_out, not_12_out, U, not_13_out);
  and and_13 (and_13_out, D0, not_14_out, not_15_out);
  and and_14 (and_14_out, D0, U, D);
  and and_15 (and_15_out, D1, not_16_out, not_17_out, D);
  and and_16 (and_16_out, D2, not_18_out, not_19_out, D);
  and and_17 (and_17_out, D2, D1, D0, not_20_out);
  or or_1 (S2, and_1_out, and_2_out, and_3_out, and_4_out, and_5_out);
  or or_2 (S1, and_6_out, and_7_out, and_8_out, and_9_out, and_10_out, and_11_out);
  or or_3 (S0, and_12_out, and_13_out, and_14_out, and_15_out, and_16_out, and_17_out);
endmodule
