// Logisim project ButtonSpeedSystem.circ as structural Verilog: 1 circuit, main circuit ButtonSpeedSystem
module ButtonSpeedSystem (
  input  U,
  input  D,
  output [2:0] Speed
);

  wire clock_1_out;
  wire [1:0] buttoninput_1_d0;
  wire [3:0] adder4bits_1_s, buttoninputconverter_1_conversion, register_1_q, sumadjuster_1_sum_2;

  ButtonInput buttoninput_1 (.U(U), .D(D), .D1(buttoninput_1_d0[1]), .D0(buttoninput_1_d0[0]));
  Register #(.width(4)) register_1 (.D(sumadjuster_1_sum_2), .Q(register_1_q), .clk(clock_1_out));  // open: en, clr
  Clock clock_1 (.out(clock_1_out));
  ButtonInputConverter buttoninputconverter_1 (
    .Button(buttoninput_1_d0), .Conversion(buttoninputconverter_1_conversion));
  Adder4Bits adder4bits_1 (.A(register_1_q), .B(buttoninputconverter_1_conversion), .S(adder4bits_1_s));  // open: COUT
  SumAdjuster sumadjuster_1 (.Sum(adder4bits_1_s), .Sum_2(sumadjuster_1_sum_2));
  BitSelector #(.width(4), .group(3)) bitselector_1 (.in(sumadjuster_1_sum_2), .out(Speed), .sel(1'b0));
endmodule
