// Logisim project ComplementBaseTwo.circ as structural Verilog: 1 circuit, main circuit ComplementBaseTwo4Bits
module ComplementBaseTwo4Bits (
  input  [3:0] A,
  output [3:0] C2
);

  wire [3:0] not_1_out;

  assign not_1_out = ~A;  // NOT_Gate not_1, 4 bits wide
  Adder4Bits adder4bits_1 (.A(not_1_out), .B(4'b0001), .S(C2));  // open: COUT
endmodule
