// Logisim project SevenSegmentRepresentation.circ as structural Verilog: 1 circuit, main circuit SevenSegmentRepresentation
module SevenSegmentRepresentation (
  input  [2:0] Number,
  output [6:0] _7SegmentNumber
);

  wire [6:0] switchthreecase7bit_1_returnedvalue, switchthreecase7bit_2_returnedvalue;

  SwitchThreeCase7Bit switchthreecase7bit_1 (
    .Value(Number), .FirstCase(3'b000), .FirstValue(7'b0111111), .SecondCase(3'b001),
    .SecondValue(7'b0000110), .ThirdCase(3'b010), .ThirdValue(7'b1011011), .DEFAULT(7'b0100111),
    .ReturnedValue(switchthreecase7bit_1_returnedvalue));
  SwitchThreeCase7Bit switchthreecase7bit_2 (
    .Value(Number), .FirstCase(3'b011), .FirstValue(7'b1001111), .SecondCase(3'b100),
    .SecondValue(7'b1100110), .ThirdCase(3'b101), .ThirdValue(7'b1101101),
    .DEFAULT(switchthreecase7bit_1_returnedvalue), .ReturnedValue(switchthreecase7bit_2_returnedvalue));
  SwitchOneCase7Bits switchonecase7bits_1 (
    .Value(Number), .FirstCase(3'b110), .FirstValue(7'b1111001),
    .Default(switchthreecase7bit_2_returnedvalue), .ReturnedValue(_7SegmentNumber));
endmodule
