// Logisim project SumAdjuster.circ as structural Verilog: 1 circuit, main circuit SumAdjuster
module SumAdjuster (
  input  [3:0] Sum,
  output [2:0] Sum_2
);

  wire bitselector_1_out, bitselector_2_out, isnonnegative_1_r, isnonnegative_2_r, not_1_out;
  wire [2:0] bitselector_3_out, multiplexer_2_out;
  wire [3:0] adder4bits_1_s;

  BitSelector #(.width(4)) bitselector_1 (.in(Sum), .out(bitselector_1_out), .sel(2'b11));
  IsNonNegative isnonnegative_1 (.Ak(bitselector_1_out), .R(isnonnegative_1_r));
  Adder4Bits adder4bits_1 (.A(Sum), .B(4'b1001), .S(adder4bits_1_s));  // open: COUT
  not not_1 (not_1_out, isnonnegative_1_r);
  IsNonNegative isnonnegative_2 (.Ak(bitselector_2_out), .R(isnonnegative_2_r));
  BitSelector #(.width(4)) bitselector_2 (.in(adder4bits_1_s), .out(bitselector_2_out), .sel(2'b11));
  BitSelector #(.width(4), .group(3)) bitselector_3 (.in(Sum), .out(bitselector_3_out), .sel(1'b0));
  Multiplexer #(.width(3)) multiplexer_1 (
    .in0(multiplexer_2_out), .in1(3'b000), .out(Sum_2), .sel(not_1_out));  // open: en
  Multiplexer #(.width(3)) multiplexer_2 (
    .in0(bitselector_3_out), .in1(3'b111), .out(multiplexer_2_out), .sel(isnonnegative_2_r));  // open: en

  // Notes on the sheet:
  //   MinSpeed
  //   MaxSpeed
endmodule
