// Logisim project Switch.circ as structural Verilog: 2 circuits, main circuit SwitchThreeCase7Bit
module SwitchThreeCase7Bit (
  input  [2:0] Value,
  input  [2:0] FirstCase,
  input  [6:0] FirstValue,
  input  [2:0] SecondCase,
  input  [6:0] SecondValue,
  input  [2:0] ThirdCase,
  input  [6:0] ThirdValue,
  input  [6:0] DEFAULT,
  output [6:0] ReturnedValue
);

  wire equality3bits_1_aqab, equality3bits_2_aqab, equality3bits_3_aqab;
  wire [6:0] ifthenelsesevenbits_1_c, ifthenelsesevenbits_2_c;

  Equality3Bits equality3bits_1 (.A(Value), .B(SecondCase), .AQAB(equality3bits_1_aqab));
  Equality3Bits equality3bits_2 (.A(Value), .B(ThirdCase), .AQAB(equality3bits_2_aqab));
  Equality3Bits equality3bits_3 (.A(Value), .B(FirstCase), .AQAB(equality3bits_3_aqab));
  IfThenElseSevenBits ifthenelsesevenbits_1 (
    .COND(equality3bits_2_aqab), .A(ThirdValue), .B(DEFAULT), .C(ifthenelsesevenbits_1_c));
  IfThenElseSevenBits ifthenelsesevenbits_2 (
    .COND(equality3bits_1_aqab), .A(SecondValue), .B(ifthenelsesevenbits_1_c), .C(ifthenelsesevenbits_2_c));
  IfThenElseSevenBits ifthenelsesevenbits_3 (
    .COND(equality3bits_3_aqab), .A(FirstValue), .B(ifthenelsesevenbits_2_c), .C(ReturnedValue));
endmodule

module SwitchOneCase7Bits (
  input  [2:0] Value,
  input  [2:0] FirstCase,
  input  [6:0] FirstValue,
  input  [6:0] Default,
  output [6:0] ReturnedValue
);

  wire equality3bits_1_aqab;

  Equality3Bits equality3bits_1 (.A(Value), .B(FirstCase), .AQAB(equality3bits_1_aqab));
  IfThenElseSevenBits ifthenelsesevenbits_1 (
    .COND(equality3bits_1_aqab), .A(FirstValue), .B(Default), .C(ReturnedValue));
endmodule
