// Logisim project IfThenElseStatements.circ as structural Verilog: 5 circuits, main circuit IfThenElseOneBit
module IfThenElseOneBit (
  input  COND,
  input  A,
  input  B,
  output C
);

  wire and_1_out, and_2_out, not_1_out;

  not not_1 (not_1_out, COND);
  and and_1 (and_1_out, not_1_out, B);
  and and_2 (and_2_out, COND, A);
  or or_1 (C, and_1_out, and_2_out);
endmodule

module IfThenElseTwoBits (
  input  COND,
  input  [1:0] A,
  input  [1:0] B,
  output [1:0] C
);

  IfThenElseOneBit ifthenelseonebit_1 (.COND(COND), .A(A[0]), .B(B[0]), .C(C[0]));
  IfThenElseOneBit ifthenelseonebit_2 (.COND(COND), .A(A[1]), .B(B[1]), .C(C[1]));
endmodule

module IfThenElseThreeBits (
  input  COND,
  input  [2:0] A,
  input  [2:0] B,
  output [2:0] C
);

  IfThenElseOneBit ifthenelseonebit_1 (.COND(COND), .A(A[2]), .B(B[2]), .C(C[2]));
  IfThenElseTwoBits ifthenelsetwobits_1 (.COND(COND), .A(A[1:0]), .B(B[1:0]), .C(C[1:0]));
endmodule

module IfThenElseFourBits (
  input  COND,
  input  [3:0] A,
  input  [3:0] B,
  output [3:0] C
);

  IfThenElseOneBit ifthenelseonebit_1 (.COND(COND), .A(A[3]), .B(B[3]), .C(C[3]));
  IfThenElseThreeBits ifthenelsethreebits_1 (.COND(COND), .A(A[2:0]), .B(B[2:0]), .C(C[2:0]));
endmodule

module IfThenElseFiveBits (
  input  COND,
  input  [4:0] A,
  input  [4:0] B,
  output [4:0] C
);

  IfThenElseOneBit ifthenelseonebit_1 (.COND(COND), .A(A[4]), .B(B[4]), .C(C[4]));
  IfThenElseFourBits ifthenelsefourbits_1 (.COND(COND), .A(A[3:0]), .B(B[3:0]), .C(C[3:0]));
endmodule
